# Fritzing sketch ESP32V2_NeoPixel_stick_noBB (saved by Fritzing 1.0.3b)

parts:
  Part2 = NeoPixel Stick [part_number=1426]
  Part3 = Adafruit ESP32 Feather V2

nets:
  GND: Part2.GND, Part3.GND
  N1: Part2.+5V, Part3.VBUS
  N2: Part2.DATAIN, Part3.IO12_A11

custom parts:
  NeoPixel Stick: Make your own little LED strip arrangement with this stick of NeoPixel LEDs. We crammed 8 of the tiny 5050 (5mm x 5mm) smart RGB LEDs onto a PCB with mounting holes and a chainable design. Use only one microcontroller pin to control as many as you can chain together! Each LED is addressable as the driver chip is inside the LED. Each one has ~18mA constant current drive so the color will be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
