# Fritzing sketch ESP32V2_NeoPixel_strip (saved by Fritzing 1.0.3b)
breadboards: 1

parts:
  Part3 = Adafruit ESP32 Feather V2
  JACK2 = 2.1mm Barrel Jack with Terminal Block
  NEOPIXEL1 = Neopixel Strip -- Black (30/m) [part_number=1376]
  R1 = Resistor [tolerance=±5% power=0.25W resistance=330 package=THT]
  C1 = Electrolytic Capacitor [capacitance=22µF voltage=35V package="200 mil [THT, electrolytic]"]

nets:
  GND: Part3.GND, JACK2.NEG, NEOPIXEL1.GND, C1.-
  N1: Part3.IO12_A11, R1.Pin_1
  N2: JACK2.POS, NEOPIXEL1.+5V
  N3: NEOPIXEL1.Din, R1.Pin_0

custom parts:
  Neopixel Strip -- Black (30/m): These NeoPixel strips have 30 digitally-addressable pixel LEDs per meter and are very affordable and are only 12.5 mm wide, 10 mm if you remove the strip from the casing.
