# Fritzing sketch ESP32V2_Motor_Transistor (saved by Fritzing 1.0.3b)
breadboards: 1

parts:
  Part1 = Adafruit ESP32 Feather V2
  M2 = DC Motor [voltage_(max)=6V voltage_(min)=3V]
  Q1 = TIP120 Hi-Current Darlington Transistor
  R1 = Resistor [tolerance=±5% power=0.25W resistance=100 package=THT]

nets:
  N1: Part1.GND, Q1.EMITTER
  N2: Part1.VBUS, M2.pin_1
  N3: Part1.IO12_A11, R1.Pin_1
  N4: M2.pin_2, Q1.COLLECTOR
  N5: Q1.BASE, R1.Pin_0
