# Fritzing sketch ESP32V2_Motor_Transistor_v2 (saved by Fritzing 1.0.3b)
breadboards: 1

parts:
  Part1 = Adafruit ESP32 Feather V2
  Q1 = TIP120 Hi-Current Darlington Transistor
  R1 = Resistor [tolerance=±5% power=0.25W resistance=100 package=THT]
  M1 = DC Motor [voltage_(max)=6V voltage_(min)=3V]
  D1 = Rectifier Diode [part_number=1N4001 package="300 mil [THT]"]

nets:
  N1: Part1.GND, Q1.EMITTER
  N2: Part1.VBUS, M1.pin_1
  N3: Part1.IO12_A11, R1.Pin_1
  N4: Q1.BASE, R1.Pin_0
  N5: Q1.COLLECTOR, M1.pin_2, D1.cathode
