# Fritzing sketch Arduino_Hbridge_2Motor_powerSupply (saved by Fritzing 1.0.3b)

parts:
  L298N1 = L298N DC motor driver
  M1 = DC Motor [voltage_(max)=6V voltage_(min)=3V]
  M2 = DC Motor [voltage_(max)=6V voltage_(min)=3V]
  Part1 = Arduino Uno (Rev3)
  VCC1 = 4 x AAA Battery Mount [internal_resistance=0.1Ω]  # not connected
  JACK1 = 2.1mm Barrel Jack with Terminal Block

nets:
  N1: L298N1.OUT1, M2.pin_2
  N2: L298N1.OUT2, M2.pin_1
  N3: L298N1.OUT3, M1.pin_2
  N4: L298N1.OUT4, M1.pin_1
  N5: L298N1.12V, JACK1.POS
  GND: L298N1.GND, Part1.GND, JACK1.NEG
  5V: L298N1.5V, Part1.5V
  N6: L298N1.ENA, Part1.D10_PWM/SS
  N7: L298N1.ENB, Part1.D5_PWM
  N8: L298N1.IN1, Part1.D9_PWM
  N9: L298N1.IN2, Part1.D8
  N10: L298N1.IN3, Part1.D7
  N11: L298N1.IN4, Part1.D6_PWM

notes:
  Left Motor
  Right Motor
  L298N Motor Driver Board

custom parts:
  L298N DC motor driver: 2x DC motor driver with 78M05 positive voltage regulator (7..35 V) L298N: max 46 V, 2 A Set 5 V Enable jumper to enable 5 V regultor (needed for the L298N) and +5 V output at screw terminal or supply external +5 V at screw terminal Set ENA and/or ENB to +5 V to enable motor permanently or supply ENA and/or ENB with PWM signal IN1 and IN2 set rotation directory for motor A (OUT1/OUT2) IN2 and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
