# Fritzing sketch ESP32V2_MotorServoNeoPixel (saved by Fritzing 1.0.3b)

parts:
  Part3 = Adafruit ESP32 Feather V2
  JACK2 = 2.1mm Barrel Jack with Terminal Block
  NEOPIXEL1 = Neopixel Strip -- Black (30/m) [part_number=1376]
  M3 = DC Motor [voltage_(max)=6V voltage_(min)=3V]  # not connected
  L298N2 = L298N DC motor driver
  J1 = Basic Servo

nets:
  GND: Part3.GND, JACK2.NEG, NEOPIXEL1.GND, L298N2.GND, J1.gnd
  +5V: Part3.VBUS, JACK2.POS, NEOPIXEL1.+5V, L298N2.12V, L298N2.5V, J1.vcc
  N1: Part3.IO12_A11, NEOPIXEL1.Din
  N2: Part3.IO33_A9, L298N2.IN2
  N3: Part3.IO15_A8, L298N2.IN1
  N4: Part3.IO32_A7, L298N2.ENA

notes:
  5V - no more, no less

custom parts:
  Neopixel Strip -- Black (30/m): These NeoPixel strips have 30 digitally-addressable pixel LEDs per meter and are very affordable and are only 12.5 mm wide, 10 mm if you remove the strip from the casing.
  L298N DC motor driver: 2x DC motor driver with 78M05 positive voltage regulator (7..35 V) L298N: max 46 V, 2 A Set 5 V Enable jumper to enable 5 V regultor (needed for the L298N) and +5 V output at screw terminal or supply external +5 V at screw terminal Set ENA and/or ENB to +5 V to enable motor permanently or supply ENA and/or ENB with PWM signal IN1 and IN2 set rotation directory for motor A (OUT1/OUT2) IN2 and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
