# Fritzing sketch ESP32V2_Servo_PwrSply (saved by Fritzing 1.0.3b)
breadboards: 1

parts:
  Part1 = Adafruit ESP32 Feather V2
  JACK1 = 2.1mm Barrel Jack with Terminal Block
  J1 = Basic Servo

nets:
  GND: Part1.GND, JACK1.NEG, J1.gnd
  N1: JACK1.POS, J1.vcc

notes:
  external power
